# Fritzing sketch rpi_temp2 (saved by Fritzing 0.9.3b)
breadboards: 1

parts:
  Raspberry_Pi_1 = Raspberry Pi B+
  DS1 = DS18B20 1-Wire Temperature Sensor [part_number=DS18B20]
  C1 = Capacitor [package=cap-pth-small-kit]

nets:
  N1: Raspberry_Pi_1.GIPO4, DS1.DQ
  GND: Raspberry_Pi_1.GND, DS1.GND, C1.1
  5V: Raspberry_Pi_1.5V, DS1.VDD, C1.2
